# Fritzing sketch schematic (saved by Fritzing 0.9.3b)

parts:
  Raspberry_Pi_1 = Raspberry Pi 3 [part_number=RPI-3-V1.2]
  Part1 = Adafruit ADS1115 16Bit I2C ADC [part_number="Adafruit #1085"]
  SONAR1 = Maxbotix MaxSonar Ultrasonic Sensor
  U1 = RJ45 Jack [package=rj45-8]
  U2 = RJ45 Jack [package=rj45-8]

nets:
  N1: Raspberry_Pi_1.GPIO2, Part1.SDA
  N2: Raspberry_Pi_1.GPIO3, Part1.SCL
  GND: Raspberry_Pi_1.GND, Part1.ADDR, Part1.GND, U1.2, U1.4, U1.6, U1.8
  5V: Raspberry_Pi_1.5V, Part1.VDD, U1.5
  N3: Part1.AIN0, U1.1
  N4: SONAR1.GND, U2.2, U2.4, U2.6, U2.8
  N5: SONAR1.+5V, U2.5
  N6: SONAR1.TX, U2.3
  N7: SONAR1.RX, U2.7
  N8: SONAR1.AN, U2.1

custom parts:
  Adafruit ADS1115 16Bit I2C ADC: For microcontrollers without an analog-to-digital converter or when you want a higher-precision ADC, the ADS1115 provides 16-bit precision at 860 samples/second over I2C. The chip can be configured as 4 single-ended input channels, or two differential channels. As a nice bonus, it even includes a programmable gain amplifier, up to x16, to help boost up smaller single/differential signals to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
  Maxbotix MaxSonar Ultrasonic Sensor: Maxbotix MaxSonar Ultrasonic Sensor LV-EZ0, LV-EZ1, LV-EZ2, LV-EZ3, LV-EZ4
